// Logisim project 4 bits somador.circ as structural Verilog
module soma_1 (
  input  A,
  input  B,
  input  C,
  output S,
  output VAI_1
);

  wire and_1_out, and_2_out, and_3_out, xor_1_out;

  and and_1 (and_1_out, A, C);
  and and_2 (and_2_out, A, B);
  and and_3 (and_3_out, B, C);
  xor xor_1 (xor_1_out, A, B);
  xor xor_2 (S, xor_1_out, C);
  or or_1 (VAI_1, and_1_out, and_2_out, and_3_out);
endmodule

module soma_4 (
  input  [3:0] in_1,
  input  [3:0] in_2,
  input  in_3,
  output out_4,
  output [3:0] out_5
);

  wire soma_1_2_vai_1, soma_1_3_vai_1, soma_1_4_vai_1;

  // Probe on in_1
  soma_1 soma_1_1 (.A(in_2[3]), .B(in_1[3]), .C(soma_1_2_vai_1), .S(out_5[3]), .VAI_1(out_4));
  soma_1 soma_1_2 (.A(in_2[2]), .B(in_1[2]), .C(soma_1_3_vai_1), .S(out_5[2]), .VAI_1(soma_1_2_vai_1));
  // Probe on out_5
  // Probe on {in_2[3:2], in_1[1], in_2[0]}
  soma_1 soma_1_3 (.A(in_1[1]), .B(in_1[1]), .C(soma_1_4_vai_1), .S(out_5[1]), .VAI_1(soma_1_3_vai_1));
  soma_1 soma_1_4 (.A(in_2[0]), .B(in_1[0]), .C(in_3), .S(out_5[0]), .VAI_1(soma_1_4_vai_1));

  assign in_2[1] = in_1[1];
endmodule
