// Logisim project 7447.circ as structural Verilog: 1 circuit, main circuit main
module main (
  input  A,
  input  B,
  input  C,
  input  D,
  output a_2,
  output b_2,
  output c_2,
  output d_2,
  output e,
  output f,
  output g
);

  wire and_1_out, and_2_out, and_3_out, and_4_out, and_5_out, and_6_out, and_7_out, and_8_out, and_9_out,
       and_10_out, and_11_out, and_12_out, and_13_out, and_14_out, and_15_out, and_16_out, and_17_out,
       and_18_out;

  and and_1 (and_1_out, ~A, ~B, ~C, D);  // AND_Gate
  and and_2 (and_2_out, ~A, B, ~C, ~D);  // AND_Gate
  and and_3 (and_3_out, A, ~B, C, ~D);  // AND_Gate
  and and_4 (and_4_out, ~A, B, C, ~D);  // AND_Gate
  nand nand_1 (c_2, ~A, ~B, C, ~D);  // NAND_Gate
  and and_5 (and_5_out, ~A, ~B, ~C, D);  // AND_Gate
  and and_6 (and_6_out, ~A, B, ~C, ~D);  // AND_Gate
  and and_7 (and_7_out, ~A, B, C, D);  // AND_Gate
  and and_8 (and_8_out, ~A, ~B, ~C, ~D);  // AND_Gate
  and and_9 (and_9_out, ~A, ~B, C, ~D);  // AND_Gate
  and and_10 (and_10_out, ~A, B, C, ~D);  // AND_Gate
  and and_11 (and_11_out, A, ~B, ~C, ~D);  // AND_Gate
  and and_12 (and_12_out, ~A, ~B, ~C, D);  // AND_Gate
  and and_13 (and_13_out, ~A, ~B, C, ~D);  // AND_Gate
  and and_14 (and_14_out, ~A, ~B, C, D);  // AND_Gate
  and and_15 (and_15_out, ~A, B, C, D);  // AND_Gate
  and and_16 (and_16_out, ~A, ~B, ~C, ~D);  // AND_Gate
  and and_17 (and_17_out, ~A, ~B, ~C, D);  // AND_Gate
  and and_18 (and_18_out, ~A, B, C, D);  // AND_Gate
  nor nor_1 (a_2, and_1_out, and_2_out);
  nor nor_2 (b_2, and_3_out, and_4_out);
  nor nor_3 (d_2, and_5_out, and_6_out, and_7_out);
  or or_1 (e, and_8_out, and_9_out, and_10_out, and_11_out);
  nor nor_4 (f, and_12_out, and_13_out, and_14_out, and_15_out);
  nor nor_5 (g, and_16_out, and_17_out, and_18_out);
endmodule
