// Logisim project EXER_1.circ as structural Verilog: 2 circuits, main circuit main
module main (
  input  B,
  input  A,
  input  C,
  output S
);

  exer_1 exer_1_1 (.A(A), .B(B), .C(C), .out_4(S));
endmodule

module exer_1 (
  input  A,
  input  B,
  input  C,
  output out_4
);

  wire and_1_out, or_1_out, xor_1_out;

  xor xor_1 (xor_1_out, A, B);
  or or_1 (or_1_out, xor_1_out, ~B);  // OR_Gate
  and and_1 (and_1_out, ~A, or_1_out);  // AND_Gate
  or or_2 (out_4, and_1_out, ~C);  // OR_Gate
endmodule
