// Logisim project aeiou.circ as structural Verilog: 1 circuit, main circuit main
module main (
  input  A,
  input  B,
  input  C,
  output A_2,
  output B_2,
  output C_2,
  output D,
  output E,
  output F,
  output G
);

  wire and_1_out;

  and and_1 (and_1_out, ~A, ~B);  // AND_Gate
  or or_1 (B_2, ~C, B);  // OR_Gate
  or or_2 (C_2, ~C, B);  // OR_Gate
  or or_3 (D, A, C);
  or or_4 (E, ~B, C);  // OR_Gate
  or or_5 (F, ~B, C);  // OR_Gate
  and and_2 (G, ~A, ~B);  // AND_Gate
  or or_6 (A_2, and_1_out, C);
endmodule
