// Logisim project dado.circ as structural Verilog: 1 circuit, main circuit main
module main (
  input  [2:0] A,
  output L1,
  output L2,
  output L3,
  output L4,
  output L5,
  output L6,
  output L7
);

  or or_1 (L1, A[2], A[1]);
  and and_1 (L2, A[2], A[1]);

  assign L3 = A[2];
  assign L4 = A[0];
  assign L5 = A[2];
  assign L6 = L2;
  assign L7 = L1;
endmodule
